# Fritzing sketch rfm01s-wiring (saved by Fritzing 0.9.3b)
breadboards: 1

parts:
  Mod1 = Raspberry Pi Pico W
  RFM12b1 = RFM12b HopeRF Transceiver
  L1 = Inductor [package="0805 [SMD]"]  # not connected

nets:
  N1: Mod1.pin_3, Mod1.pin_8, Mod1.pin_13, Mod1.pin_18, Mod1.pin_23, Mod1.pin_28, Mod1.pin_33, Mod1.pin_38, RFM12b1.10_GND
  N2: Mod1.pin_15, RFM12b1.3_FSK/DATA
  N3: Mod1.pin_21, RFM12b1.1_SDO
  N4: Mod1.pin_25, RFM12b1.12_SDI

custom parts:
  Raspberry Pi Pico W: Raspberry Pi Pico W. Based around the RP2040 microcontroller the Pico W is a low cost microcontroller device bringing Raspberry Pi quality, cost, and easy of use to the microcontroller space. The areas marked KEEPOUT in pcb silkscreen should not have traces running through them to avoid shorts on a soldered in module!
